# Fritzing sketch wiring-temp-and-leds (saved by Fritzing 0.9.9b)
breadboards: 2

parts:
  Mod1 = Heltec WiFi LoRa 32 V2 [part_number=HTIT-WB32LA]
  Part1 = MCP9808 High Accuracy I2C Temperature Sensor [part_number=1782]
  LED1 = smd LED [color="Red (633nm)" package="0805 [SMD]"]
  LED2 = smd LED [color="Yellow (595nm)" package="0805 [SMD]"]
  LED3 = smd LED [color="Green (565nm)" package="0805 [SMD]"]
  R1 = Resistor [tolerance=±5% resistance=220 package="0402 [SMD]"]
  R2 = Resistor [tolerance=±5% resistance=220 package="0402 [SMD]"]
  R3 = Resistor [tolerance=±5% resistance=220 package="0402 [SMD]"]
  Mod2 = Heltec WiFi LoRa 32 V2 [part_number=HTIT-WB32LA]
  Part2 = MCP9808 High Accuracy I2C Temperature Sensor [part_number=1782]
  LED4 = smd LED [color="Red (633nm)" package="0805 [SMD]"]
  LED5 = smd LED [color="Yellow (595nm)" package="0805 [SMD]"]
  LED6 = smd LED [color="Green (560nm)" package="0805 [SMD]"]
  R4 = Resistor [tolerance=±5% resistance=220 package="0402 [SMD]"]
  R5 = Resistor [tolerance=±5% resistance=220 package="0402 [SMD]"]
  R6 = Resistor [tolerance=±5% resistance=220 package="0402 [SMD]"]

nets:
  N1: Mod1.pin_1, Part1.SDA
  N2: Mod1.pin_2, R2.Pin_1
  N3: Mod1.pin_3, R1.Pin_1
  N4: Mod1.pin_4, R3.Pin_1
  N5: Mod1.GND, LED1.cathode, LED2.cathode, LED3.cathode
  N6: Mod1.pin_20, Part1.VDD
  N7: Mod1.pin_27, Part1.SCL
  N8: LED1.anode, R1.Pin_0
  N9: LED2.anode, R2.Pin_0
  N10: LED3.anode, R3.Pin_0
  N11: Mod2.pin_1, Part2.SDA
  N12: Mod2.pin_2, R5.Pin_0
  N13: Mod2.pin_3, R4.Pin_0
  N14: Mod2.pin_4, R6.Pin_0
  N15: Mod2.pin_16, Mod2.pin_17
  GND: Mod2.GND, Part2.GND, LED4.cathode, LED5.cathode, LED6.cathode, R6.Pin_1
  N16: Mod2.pin_20, Part2.VDD
  N17: Mod2.pin_21, Mod2.pin_22
  N18: Mod2.pin_27, Part2.SCL
  N19: LED4.anode, R4.Pin_1
  N20: LED5.anode, R5.Pin_1

notes:
  compact
  spacious

custom parts:
  MCP9808 High Accuracy I2C Temperature Sensor: This I2C digital temperature sensor is one of the more accurate/precise we've ever seen, with a typical accuracy of ±0.25°C over the sensor's -40°C to +125°C range and precision of +0.0625°C. They work great with any microcontroller using standard i2c. There are 3 address pins so you can connect up to 8 to a single I2C bus without address collisions. Best of all, a wide voltage range makes is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
