# Fritzing sketch wiring-temp-and-leds_schem (saved by Fritzing 0.9.9b)
breadboards: 1

parts:
  Mod2 = Heltec WiFi LoRa 32 V2 [part_number=HTIT-WB32LA]
  Part2 = MCP9808 High Accuracy I2C Temperature Sensor [part_number=1782]

nets:
  N1: Mod2.pin_16, Mod2.pin_17
  GND: Mod2.GND, Part2.GND
  N2: Mod2.pin_20, Part2.VDD
  N3: Mod2.pin_21, Mod2.pin_22
  N4: Mod2.pin_27, Part2.SCL
  N5: Mod2.pin_29, Part2.SDA

custom parts:
  MCP9808 High Accuracy I2C Temperature Sensor: This I2C digital temperature sensor is one of the more accurate/precise we've ever seen, with a typical accuracy of ±0.25°C over the sensor's -40°C to +125°C range and precision of +0.0625°C. They work great with any microcontroller using standard i2c. There are 3 address pins so you can connect up to 8 to a single I2C bus without address collisions. Best of all, a wide voltage range makes is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
